# Fritzing sketch Embedded_Innlevering1 (saved by Fritzing 0.8.3b)
breadboards: 4

parts:
  Part1 = Arduino Uno (Rev3)
  R1 = Resistor [tolerance=±5% resistance=220 package=THT]
  R2 = Resistor [tolerance=±5% resistance=220 package=THT]
  R3 = Resistor [tolerance=±5% resistance=220 package=THT]
  R4 = Resistor [tolerance=±5% resistance=220 package=THT]
  R5 = Resistor [tolerance=±5% resistance=220 package=THT]
  R6 = Resistor [tolerance=±5% resistance=220 package=THT]
  R7 = Resistor [tolerance=±5% resistance=220 package=THT]
  R8 = Resistor [tolerance=±5% resistance=220 package=THT]
  U1 = MAX7219 [package=dil24]
  Part2 = Arduino Uno (Rev3)
  R9 = Resistor [tolerance=±5% resistance=220 package=THT]
  R10 = Resistor [tolerance=±5% resistance=220 package=THT]
  R11 = Resistor [tolerance=±5% resistance=220 package=THT]
  R12 = Resistor [tolerance=±5% resistance=220 package=THT]
  R13 = Resistor [tolerance=±5% resistance=220 package=THT]
  R14 = Resistor [tolerance=±5% resistance=220 package=THT]
  R15 = Resistor [tolerance=±5% resistance=220 package=THT]
  R16 = Resistor [tolerance=±5% resistance=220 package=THT]
  U2 = MAX7219 [package=dil24]

nets:
  N1: Part1.ICSP_MISO, Part1.D12/MISO, U1.DIN
  N2: Part1.ICSP_MOSI, Part1.D11_PWM/MOSI, U1.CLK
  N3: Part1.D10_PWM/SS, U1.LOAD
  5V: Part1.5V, U1.VCC
  GND: Part1.GND, U1.GND, U1.GND2
  N4: R1.Pin_1, U1.SEGDP
  N5: R2.Pin_1, U1.SEGA
  N6: R3.Pin_1, U1.SEGB
  N7: R4.Pin_1, U1.SEGC
  N8: R5.Pin_1, U1.SEGG
  N9: R6.Pin_1, U1.SEGF
  N10: R7.Pin_1, U1.SEGE
  N11: R8.Pin_1, U1.SEGD
  N12: Part2.ICSP_MISO, Part2.D12/MISO, U2.DIN
  N13: Part2.ICSP_MOSI, Part2.D11_PWM/MOSI, U2.CLK
  N14: Part2.D10_PWM/SS, U2.LOAD
  5V_2: Part2.5V, U2.VCC
  GND_2: Part2.GND, U2.GND, U2.GND2
  N15: R9.Pin_1, U2.SEGDP
  N16: R10.Pin_1, U2.SEGD
  N17: R11.Pin_1, U2.SEGF
  N18: R12.Pin_1, U2.SEGG
  N19: R13.Pin_1, U2.SEGE
  N20: R14.Pin_1, U2.SEGA
  N21: R15.Pin_1, U2.SEGC
  N22: R16.Pin_1, U2.SEGB

notes:
  16
  8x8 LED Matrix
  1
  Bruke røde lysdioder
  Bruker grønne lysdioder
